// Logisim project LeMinhChi_6551071011.circ as structural Verilog: 1 circuit, main circuit main
module main (
  input  in_1,
  input  in_2,
  output out_3,
  output out_4,
  output out_5,
  output out_6,
  output out_7,
  output out_8,
  output out_9
);

  and and_1 (out_3, in_1, in_2);
  or or_1 (out_4, in_1, in_2);
  not not_1 (out_5, in_1);
  xor xor_1 (out_6, in_1, in_2);
  xnor xnor_1 (out_7, in_1, in_2);
  nand nand_1 (out_8, in_1, in_2);
  nor nor_1 (out_9, in_1, in_2);
endmodule
