// Logisim project LeMinhChi_6551071011_C1.circ as structural Verilog: 1 circuit, main circuit main
module main (
  input  A0,
  input  A1,
  input  A2,
  input  EN,
  output Y0,
  output Y1,
  output Y2,
  output Y3,
  output Y4,
  output Y5,
  output Y6,
  output Y7
);

  Decoder #(.select(3)) decoder_1 (
    .out0(Y0), .out1(Y1), .out2(Y2), .out3(Y3), .out4(Y4), .out5(Y5), .out6(Y6), .out7(Y7),
    .sel({A0, A1, A2}), .en(EN));
endmodule
