// Logisim project LeMinhChi_6551071011_C3.circ as structural Verilog: 1 circuit, main circuit main
module main (
  input  [3:0] A,
  input  [3:0] B,
  output [3:0] SUM,
  output out_4
);

  Adder #(.width(4)) adder_1 (.a(A), .b(B), .out(SUM), .cin(1'b0), .cout(out_4));
endmodule
