// Logisim project LeMinhChi_6551071011_C5.circ as structural Verilog: 1 circuit, main circuit main
module main (
  input  [3:0] A,
  input  [3:0] B,
  output out_3,
  output out_4,
  output out_5
);

  Comparator #(.width(4)) comparator_1 (.a(A), .b(B), .gt(out_3), .eq(out_4), .lt(out_5));
endmodule
