// Logisim project LeMinhChi_6551071011_C6.circ as structural Verilog: 1 circuit, main circuit main
module main (
  input  Reset,
  input  Enable,
  output out_3,
  output out_4,
  output out_5,
  output out_6
);

  wire clock_1_out, Q0_qn, Q1_qn, Q2_qn, Q3_qn;

  Clock clock_1 (.out(clock_1_out));
  D_Flip_Flop #(.trigger("falling")) Q0 (
    .clk(clock_1_out), .D(Q0_qn), .Q(out_3), .Qn(Q0_qn), .preset(1'b0), .en(Enable), .reset(Reset));
  D_Flip_Flop #(.trigger("falling")) Q1 (
    .clk(out_3), .D(Q1_qn), .Q(out_4), .Qn(Q1_qn), .preset(1'b0), .en(Enable), .reset(Reset));
  D_Flip_Flop #(.trigger("falling")) Q2 (
    .clk(out_4), .D(Q2_qn), .Q(out_5), .Qn(Q2_qn), .preset(1'b0), .en(Enable), .reset(Reset));
  D_Flip_Flop #(.trigger("falling")) Q3 (
    .clk(out_5), .D(Q3_qn), .Q(out_6), .Qn(Q3_qn), .preset(1'b0), .en(Enable), .reset(Reset));
endmodule
