// Logisim project LeMinhChi_6551071011_C7.circ as structural Verilog: 1 circuit, main circuit main
module main (
  input  [2:0] Address,
  input  [3:0] Data_in,
  input  Write,
  input  Read,
  output [3:0] Out
);

  wire clock_1_out;

  Clock clock_1 (.out(clock_1_out));
  RAM #(.addrWidth(3), .dataWidth(4), .bus("separate")) ram_1 (
    .addr(Address), .din(Data_in), .data(Out), .str(Write), .sel(1'b1), .clk(clock_1_out), .ld(Read));  // open: clr
endmodule
