// Logisim project LeMinhChi_6551071011_Câu3b.circ as structural Verilog: 1 circuit, main circuit main
module main (
  input  E,
  input  D,
  input  D_2,
  output out_4,
  output out_5
);

  wire CLK_out;

  Clock CLK (.out(CLK_out));
  D_Flip_Flop #(.trigger("high")) d_ff_1 (
    .clk(E), .D(D), .Q(out_4), .preset(1'b0), .en(1'b1), .reset(1'b0));  // open: Qn
  T_Flip_Flop t_ff_1 (.clk(CLK_out), .T(D_2), .Q(out_5), .preset(1'b0), .reset(1'b0), .en(1'b1));  // open: Qn
endmodule
